# Fritzing sketch sketch (saved by Fritzing 0.9.3b)
breadboards: 1

parts:
  Part1 = Arduino Uno (Rev3) - ICSP
  RE1 = Rotary Encoder [package=THT]
  RE2 = Rotary Encoder [package=THT]
  U2 = SWITCH_SPDT [package=kps-1290]
  U3 = SWITCH_SPDT [package=kps-1290]
  U4 = SWITCH_SPDT [package=kps-1290]
  U5 = SWITCH_SPDT [package=kps-1290]
  R1 = Resistor [tolerance=±5% resistance=220 package="0402 [SMD]"]
  R2 = Resistor [tolerance=±5% resistance=220 package="0402 [SMD]"]
  R3 = Resistor [tolerance=±5% resistance=220 package="0402 [SMD]"]
  R4 = Resistor [tolerance=±5% resistance=220 package="0402 [SMD]"]

nets:
  N1: Part1.A0, U2.S, R4.Pin_1
  N2: Part1.A1, U4.S, R3.Pin_1
  N3: Part1.A2, U3.S, R2.Pin_1
  N4: Part1.A3, U5.S, R1.Pin_1
  N5: Part1.D0/RX, RE2.EncoderPinA
  N6: Part1.D1/TX, RE2.EncoderPinB
  N7: Part1.D2, RE1.EncoderPinB
  N8: Part1.D3_PWM, RE1.EncoderPinA
  N9: Part1.5V, RE1.EncoderPinC, RE2.EncoderPinC, U2.O, U3.O, U4.O, U5.O
  N10: Part1.GND, R1.Pin_0, R2.Pin_0, R3.Pin_0, R4.Pin_0

notes:
  load
